# Fritzing sketch schéma_projet (saved by Fritzing 0.9.3b)
breadboards: 1

parts:
  R1 = Rotary Potentiometer (Small) [maximum_resistance=100kΩ package=THT]
  U1 = NodeMCU V1.0
  LED1 = LED - 5mm [color="Red (633nm)" package="5 mm [THT]"]
  R2 = Resistor [tolerance=±5% resistance=220 package=THT]

nets:
  N1: R1.leg1, U1.CMD
  N2: R1.wiper, U1.A0
  N3: R1.leg2, U1.SD1
  N4: U1.D1, LED1.cathode
  N5: U1.3V3, R2.Pin_0
  N6: LED1.anode, R2.Pin_1

custom parts:
  NodeMCU V1.0: ESP8266 based NodeMCU
